// Logisim project Chips.circ as structural Verilog: 4 circuits, main circuit TTTC
module TTTC (
  input  btn,
  input  [1:0] vin,
  input  [1:0] hin,
  output vout,
  output hout,
  output [3:0] L0,
  output [3:0] L1,
  output [3:0] L2,
  output [3:0] L3
);

  wire and_1_out, nor_1_out;
  wire [1:0] register_1_q;
  wire [15:0] bitselector_1_out;

  Pull_Resistor pull_resistor_1 (.node(hin[0]));
  Pull_Resistor pull_resistor_2 (.node(vin[0]));
  Pull_Resistor pull_resistor_3 (.node(vin[1]));
  Pull_Resistor pull_resistor_4 (.node(hin[1]));
  and and_1 (and_1_out, hin[1], vin[1]);
  Register #(.width(2), .trigger("low")) register_1 (
    .D({vin[0], hin[0]}), .en(and_1_out), .Q(register_1_q), .clk(1'b0));  // open: clr
  nor nor_1 (nor_1_out, register_1_q[1], register_1_q[0]);
  BitSelector #(.width(32), .group(16)) bitselector_1 (
    .in(32'h9429f99f), .out(bitselector_1_out), .sel(register_1_q[1]));
  BitSelector #(.width(32), .group(16)) bitselector_2 (
    .in({{16{1'b0}}, bitselector_1_out}), .out({L3, L2, L1, L0}), .sel(nor_1_out));
  Transistor #(.\type ("n")) transistor_1 (.in(btn), .out(hout), .gate(btn));
  // Probe on {L3, L2, L1, L0}

  assign vout = hout;
endmodule

module BPC (
  input  V0,
  input  V1,
  input  V2,
  input  H0,
  input  H1,
  input  H2,
  input  enable,
  output ready,
  output [3:0] XY
);

  wire not_1_out, not_2_out, or_1_out, or_2_out;
  wire [1:0] bitselector_1_out, bitselector_2_out;

  Pull_Resistor pull_resistor_1 (.node(V2));
  Pull_Resistor pull_resistor_2 (.node(V0));
  Pull_Resistor pull_resistor_3 (.node(V1));
  not not_1 (not_1_out, V0);
  not not_2 (not_2_out, H0);
  Pull_Resistor pull_resistor_4 (.node(H1));
  Pull_Resistor pull_resistor_5 (.node(H0));
  Pull_Resistor pull_resistor_6 (.node(H2));
  BitSelector #(.width(4), .group(2)) bitselector_1 (.in({V2, V1, 2'b00}), .out(bitselector_1_out), .sel(not_1_out));
  BitSelector #(.width(4), .group(2)) bitselector_2 (.in({H2, H1, 2'b00}), .out(bitselector_2_out), .sel(not_2_out));
  or or_1 (or_1_out, H0, H1, H2);
  or or_2 (or_2_out, V0, V1, V2);
  and and_1 (ready, or_2_out, or_1_out, enable);
  assign XY = enable ? {bitselector_2_out, bitselector_1_out} : 4'bz;  // Controlled_Buffer controlled_buffer_1
  Pull_Resistor pull_resistor_7 (.node(XY));
endmodule

module SDR (
  input  [1:0] symID,
  input  [3:0] XY,
  input  Enable,
  output [1:0] H0,
  output [1:0] H1,
  output [1:0] H2,
  output [1:0] V0,
  output [1:0] V1,
  output [1:0] V2
);

  wire [3:0] bitselector_1_out;

  BitSelector #(.group(4)) bitselector_1 (.in({XY, 4'b1111}), .out(bitselector_1_out), .sel(Enable));
  BitSelector #(.width(9), .group(3)) bitselector_2 (
    .in(9'h111), .out({V2[1], V1[1], V0[1]}), .sel(bitselector_1_out[1:0]));
  BitSelector #(.width(9), .group(3)) bitselector_3 (
    .in(9'h111), .out({H2[1], H1[1], H0[1]}), .sel(bitselector_1_out[3:2]));

  assign H0[0] = symID[0];
  assign H1[0] = symID[0];
  assign H2[0] = symID[0];
  assign V0[0] = symID[1];
  assign V1[0] = symID[1];
  assign V2[0] = symID[1];
endmodule

module GSDD (
  input  [1:0] score,
  input  clock,
  output win,
  output lose,
  output draw
);

  wire [1:0] register_1_q;

  Pull_Resistor pull_resistor_1 (.node(clock));
  Register #(.width(2), .trigger("high")) register_1 (
    .D(score), .en(clock), .Q(register_1_q), .clk(clock));  // open: clr
  Decoder #(.select(2), .enable("false")) decoder_1 (
    .out1(win), .out2(lose), .out3(draw), .sel(register_1_q));  // open: out0
  Pull_Resistor pull_resistor_2 (.node(draw));
  Pull_Resistor pull_resistor_3 (.node(win));
  Pull_Resistor pull_resistor_4 (.node(lose));
endmodule
